# Fritzing sketch electronic_scheme (saved by Fritzing 0.9.4)
breadboards: 1

parts:
  R1 = Resistor [tolerance=±5% resistance=1k package=THT]
  ESP12e = ESP 12E
  R2 = Resistor [tolerance=±5% resistance=1k package=THT]
  S1 = Pushbutton [package=THT]
  S2 = Pushbutton [package=THT]
  R3 = Resistor [tolerance=±5% resistance=10k package=THT]
  R4 = Resistor [tolerance=±5% resistance=10k package=THT]
  Q1 = Basic FET N-Channel [package="TO220 [THT]"]
  Q2 = Basic FET N-Channel [package="TO220 [THT]"]
  R5 = Resistor [tolerance=±5% resistance=10k package=THT]
  R6 = Resistor [tolerance=±5% resistance=10k package=THT]
  J1 = shrouded pin header, 6 pins [form="♂ (shrouded male)"]
  Buck_converter = Mini-360 DC-DC Buck converter [package=THT]

nets:
  N1: R1.Pin_0, ESP12e.GND, R3.Pin_1, R4.Pin_1, Q1.source, Q2.source, R5.Pin_1, R6.Pin_1, Buck_converter.OUT-
  N2: R1.Pin_1, ESP12e.GPIO15
  N3: ESP12e.GPIO5, S1.leg0, R3.Pin_0
  N4: ESP12e.GPIO2, Q1.gate, R6.Pin_0
  N5: ESP12e.VCC, R2.Pin_0, S1.leg1, S2.leg1, Buck_converter.OUT+
  N6: ESP12e.GPIO13, S2.leg0, R4.Pin_0
  N7: ESP12e.GPIO16, Q2.gate, R5.Pin_0
  N8: ESP12e.EN, R2.Pin_1
  N9: Q1.drain, J1.pin5
  N10: Q2.drain, J1.pin4
  N11: J1.pin2, Buck_converter.IN-
  N12: J1.pin6, Buck_converter.IN+

notes:
  RELAY_DOWN (GPIO16)
  RELAY_UP (GPIO2)
  BUTTON_UP (GPIO5)
  BUTTON_DOWN (GPIO13)

custom parts:
  ESP 12E: ESP 12e module with spi interface and wifi connection
  Mini-360 DC-DC Buck converter: Mini-360 DC-DC Buck converter. Tiny buck step down voltage converter, input voltage 4.75 to 23V output 1 to 17V adjustable. Available from ebay and the like.
